# Fritzing sketch arduino-bluetooth-relay (saved by Fritzing 0.9.3b)
breadboards: 1

parts:
  Parça1 = Arduino Uno (Rev3)
  Parça2 = Bluetooth HC-05 Macho
  Mod1 = KY-019 5V Relay Module [package="Breakout board"]

nets:
  N1: Parça1.D0/RX, Parça2.RXD
  N2: Parça1.D1/TX, Parça2.TXD
  N3: Parça1.D6_PWM, Mod1.S
  5V: Parça1.5V, Parça2.VCC, Mod1.+
  GND: Parça1.GND, Parça2.GND

custom parts:
  KY-019 5V Relay Module: KY-019 5V Relay module, used to control AC circuits.
